# Fritzing sketch 2018_03_27_Schematics (saved by Fritzing 0.9.3b)
breadboards: 1

parts:
  Componente1 = MPR121 Breakout
  Componente2 = Arduino Uno (Rev3)
  C1 = Electrolytic Capacitor [capacitance=1mF package="100 mil [THT, electrolytic]"]
  R1 = Resistor [tolerance=±5% resistance=220 package=THT]
  R2 = Resistor [tolerance=±5% resistance=220 package=THT]

nets:
  N1: Componente1.SCL, Componente2.A5/SCL
  N2: Componente1.SDA, Componente2.A4/SDA
  3.3V: Componente1.3.3V, Componente2.5V
  GND: Componente1.GND, Componente2.GND, C1.-
  N3: Componente2.D4, R1.Pin_0
  N4: Componente2.D5_PWM, R2.Pin_0

notes:
  1000uF 6.3V
  5V power supply
  Adafruit MPR121 can be connected directly to Arduino 5V rail
  DOTSTAR led strip
  GND
  Vcc
  data pin
  clock pin
